# Fritzing sketch PIR Basic (saved by Fritzing 0.9.3b)

parts:
  LED1 = smd LED [color="Red (633nm)" package="1206 [SMD]"]
  Part1 = Arduino Leonardo (Rev3b)
  PIR1 = PIR sensor
  VCC1 = Battery block 9V

nets:
  GND: LED1.cathode, Part1.GND, PIR1.GND, VCC1.-
  N1: LED1.anode, Part1.D13_PWM
  N2: Part1.D7, PIR1.SIG
  5V: Part1.5V, PIR1.VDD, VCC1.+
